# Fritzing sketch HC-05 Layout (saved by Fritzing 0.9.2b)

parts:
  Pro_Micro1 = Pro Micro
  Part2 = Bluetooth HC-05 Macho

nets:
  N1: Pro_Micro1.TX1, Part2.RXD
  N2: Pro_Micro1.RX0, Part2.TXD
  GND: Pro_Micro1.GND, Part2.GND
  N3: Pro_Micro1.D9, Part2.Key
  VCC: Pro_Micro1.VCC, Part2.VCC

custom parts:
  Pro Micro: The SparkFun Pro Micro is a complete USB-based microcontoller development system, in a very small footprint, capable of implementing many types of projects. All programming can be done via the USB port.
